// Logisim project LC-2200-16.circ as structural Verilog: 4 circuits, main circuit main
module main (
  output [3:0] out_1,
  output [3:0] out_2
);

  wire CLK, CLR, comparator_1_eq, DrALU, DrMEM, DrOFF, DrPC, DrReg, LdA, LdB, LdIR, LdMAR, LdPC, LdZ, WrMEM,
       WrREG, Z;
  wire [0:0] IR_q;
  wire [1:0] func, RegSel;
  wire [2:0] OPCODE;
  wire [3:0] IR_q_2, IR_q_3, IR_q_4;
  wire [15:0] A_q, alu_1_out_4, B_q, bit_extender_1_out, controlled_buffer_1_out, MAR_q, PC_q, ram_1_data,
       registers_1_data_out;

  Register #(.width(16)) PC (.D(controlled_buffer_1_out), .en(LdPC), .Q(PC_q), .clk(CLK), .clr(CLR));
  assign controlled_buffer_1_out = DrPC ? PC_q : 16'bz;  // Controlled_Buffer controlled_buffer_1
  Register #(.width(16)) A (.D(controlled_buffer_1_out), .en(LdA), .Q(A_q), .clk(CLK), .clr(CLR));
  ALU alu_1 (.in_3(func), .A(A_q), .B(B_q), .out_4(alu_1_out_4));
  assign controlled_buffer_1_out = DrALU ? alu_1_out_4 : 16'bz;  // Controlled_Buffer controlled_buffer_2
  Comparator #(.width(16)) comparator_1 (
    .a(controlled_buffer_1_out), .b({16{1'b0}}), .eq(comparator_1_eq));  // open: gt, lt
  Register #(.width(1)) Z_Register (.D(comparator_1_eq), .en(LdZ), .Q(Z), .clk(CLK), .clr(CLR));
  Clock clock_1 (.out(CLK));
  Button button_1 (.out(CLR));
  Register #(.width(16)) B (.D(controlled_buffer_1_out), .en(LdB), .Q(B_q), .clk(CLK), .clr(CLR));
  Registers registers_1 (
    .in_1(controlled_buffer_1_out), .in_2(CLK), .in_3(CLR), .WrREG(WrREG), .RegNo(out_1),
    .Data_Out(registers_1_data_out));
  assign controlled_buffer_1_out = DrReg ? registers_1_data_out : 16'bz;  // Controlled_Buffer controlled_buffer_3
  Microcontrol_Unit microcontrol_unit_1 (
    .OPCODE(OPCODE), .Z(Z), .CLK(CLK), .CLR(CLR), .DrREG(DrReg), .DrMEM(DrMEM), .DrALU(DrALU), .DrPC(DrPC),
    .DrOFF(DrOFF), .LdPC(LdPC), .LdIR(LdIR), .LdMAR(LdMAR), .LdA(LdA), .LdB(LdB), .LdZ(LdZ), .WrREG(WrREG),
    .WrMEM(WrMEM), .RegSel(RegSel), .func(func));
  Register #(.width(16)) MAR (.D(controlled_buffer_1_out), .en(LdMAR), .Q(MAR_q), .clk(CLK), .clr(CLR));
  Register #(.width(16)) IR (
    .D(controlled_buffer_1_out), .en(LdIR), .Q({OPCODE, IR_q_4, IR_q_3, IR_q_2, IR_q[0]}), .clk(CLK),
    .clr(CLR));
  RAM #(.addrWidth(16), .dataWidth(16), .bus("separate")) ram_1 (
    .addr(MAR_q), .din(controlled_buffer_1_out), .data(ram_1_data), .str(WrMEM), .sel(1'b1), .clk(CLK),
    .ld(1'b1), .clr(CLR));
  assign controlled_buffer_1_out = DrMEM ? ram_1_data : 16'bz;  // Controlled_Buffer controlled_buffer_4
  Multiplexer #(.select(2), .width(4), .enable("false")) multiplexer_1 (
    .in0(IR_q_4), .in1(IR_q_3), .in2(IR_q_2), .out(out_1), .sel(RegSel));  // open: in3
  assign controlled_buffer_1_out = DrOFF ? bit_extender_1_out : 16'bz;  // Controlled_Buffer controlled_buffer_5
  assign bit_extender_1_out = {{11{IR_q_2[3]}}, {IR_q_2, IR_q[0]}};  // Bit_Extender bit_extender_1

  assign out_2 = out_1;

  // Other names for the same wires on the sheet: RegNo[3:0] = out_1

  // Notes on the sheet:
  //   Jongyeon Kim
  //   903018469
endmodule

// RegFile
module Registers (
  input  [15:0] in_1,
  input  in_2,
  input  in_3,
  input  WrREG,
  input  [3:0] RegNo,
  output [15:0] Data_Out
);

  wire and_1_out, and_2_out, and_3_out, and_4_out, and_5_out, and_6_out, and_7_out, and_8_out, and_9_out,
       and_10_out, and_11_out, and_12_out, and_13_out, and_14_out, and_15_out, and_16_out, decoder_1_out0,
       decoder_1_out1, decoder_1_out2, decoder_1_out3, decoder_1_out4, decoder_1_out5, decoder_1_out6,
       decoder_1_out7, decoder_1_out8, decoder_1_out9, decoder_1_out10, decoder_1_out11, decoder_1_out12,
       decoder_1_out13, decoder_1_out14, decoder_1_out15;
  wire [15:0] a0, a1, a2, at, fp, k0, ra, s0, s1, s2, sp, t0, t1, t2, v0, zero;

  Decoder #(.select(4), .enable("false")) decoder_1 (
    .out0(decoder_1_out0), .out1(decoder_1_out1), .out2(decoder_1_out2), .out3(decoder_1_out3),
    .out4(decoder_1_out4), .out5(decoder_1_out5), .out6(decoder_1_out6), .out7(decoder_1_out7),
    .out8(decoder_1_out8), .out9(decoder_1_out9), .out10(decoder_1_out10), .out11(decoder_1_out11),
    .out12(decoder_1_out12), .out13(decoder_1_out13), .out14(decoder_1_out14), .out15(decoder_1_out15),
    .sel(RegNo));
  and and_1 (and_1_out, decoder_1_out0, WrREG);
  and and_2 (and_2_out, decoder_1_out1, WrREG);
  and and_3 (and_3_out, decoder_1_out2, WrREG);
  and and_4 (and_4_out, decoder_1_out3, WrREG);
  and and_5 (and_5_out, decoder_1_out4, WrREG);
  and and_6 (and_6_out, decoder_1_out5, WrREG);
  and and_7 (and_7_out, decoder_1_out6, WrREG);
  and and_8 (and_8_out, decoder_1_out7, WrREG);
  and and_9 (and_9_out, decoder_1_out8, WrREG);
  and and_10 (and_10_out, decoder_1_out9, WrREG);
  and and_11 (and_11_out, decoder_1_out10, WrREG);
  and and_12 (and_12_out, decoder_1_out11, WrREG);
  and and_13 (and_13_out, decoder_1_out12, WrREG);
  and and_14 (and_14_out, decoder_1_out13, WrREG);
  and and_15 (and_15_out, decoder_1_out14, WrREG);
  and and_16 (and_16_out, decoder_1_out15, WrREG);
  Register #(.width(16)) u_zero (.D(in_1), .en(and_1_out), .Q(zero), .clk(in_2), .clr(1'b1));
  Register #(.width(16)) u_at (.D(in_1), .en(and_2_out), .Q(at), .clk(in_2), .clr(in_3));
  Register #(.width(16)) u_v0 (.D(in_1), .en(and_3_out), .Q(v0), .clk(in_2), .clr(in_3));
  Register #(.width(16)) u_a0 (.D(in_1), .en(and_4_out), .Q(a0), .clk(in_2), .clr(in_3));
  Register #(.width(16)) u_a1 (.D(in_1), .en(and_5_out), .Q(a1), .clk(in_2), .clr(in_3));
  Register #(.width(16)) u_a2 (.D(in_1), .en(and_6_out), .Q(a2), .clk(in_2), .clr(in_3));
  Register #(.width(16)) u_t0 (.D(in_1), .en(and_7_out), .Q(t0), .clk(in_2), .clr(in_3));
  Register #(.width(16)) u_t1 (.D(in_1), .en(and_8_out), .Q(t1), .clk(in_2), .clr(in_3));
  Register #(.width(16)) u_t2 (.D(in_1), .en(and_9_out), .Q(t2), .clk(in_2), .clr(in_3));
  Register #(.width(16)) u_s0 (.D(in_1), .en(and_10_out), .Q(s0), .clk(in_2), .clr(in_3));
  Register #(.width(16)) u_s1 (.D(in_1), .en(and_11_out), .Q(s1), .clk(in_2), .clr(in_3));
  Register #(.width(16)) u_s2 (.D(in_1), .en(and_12_out), .Q(s2), .clk(in_2), .clr(in_3));
  Register #(.width(16)) u_k0 (.D(in_1), .en(and_13_out), .Q(k0), .clk(in_2), .clr(in_3));
  Register #(.width(16)) u_sp (.D(in_1), .en(and_14_out), .Q(sp), .clk(in_2), .clr(in_3));
  Register #(.width(16)) u_fp (.D(in_1), .en(and_15_out), .Q(fp), .clk(in_2), .clr(in_3));
  Register #(.width(16)) u_ra (.D(in_1), .en(and_16_out), .Q(ra), .clk(in_2), .clr(in_3));
  Multiplexer #(.select(4), .width(16), .enable("false")) multiplexer_1 (
    .in0(zero), .in1(at), .in2(v0), .in3(a0), .in4(a1), .in5(a2), .in6(t0), .in7(t1), .in8(t2), .in9(s0),
    .in10(s1), .in11(s2), .in12(k0), .in13(sp), .in14(fp), .in15(ra), .out(Data_Out), .sel(RegNo));

  // Other names for the same wires on the sheet: CLK = in_2; CLR = in_3; Data_In[15:0] = in_1

  // Notes on the sheet:
  //   Jongyeon Kim
  //   903018469
endmodule

module ALU (
  input  [15:0] A,
  input  [15:0] B,
  input  [1:0] in_3,
  output [15:0] out_4
);

  wire [15:0] adder_1_out, adder_2_out, nand_1_out, subtractor_1_out;

  Adder #(.width(16)) adder_1 (.a(A), .b(B), .out(adder_1_out));  // open: cin, cout
  assign nand_1_out = ~(A & B);  // NAND_Gate nand_1, 16 bits wide
  Multiplexer #(.select(2), .width(16), .enable("false")) multiplexer_1 (
    .in0(adder_1_out), .in1(nand_1_out), .in2(subtractor_1_out), .in3(adder_2_out), .out(out_4), .sel(in_3));
  Subtractor #(.width(16)) subtractor_1 (.a(A), .b(B), .out(subtractor_1_out));  // open: bin, bout
  Adder #(.width(16)) adder_2 (.a(A), .b(16'h1), .out(adder_2_out));  // open: cin, cout

  // Notes on the sheet:
  //   00 ADD
  //   01 NAND
  //   10 A-B
  //   11 A+1
  //   Jongyeon Kim
  //   903018469
endmodule

module Microcontrol_Unit (
  input  [2:0] OPCODE,
  input  Z,
  input  CLK,
  input  CLR,
  output DrREG,
  output DrMEM,
  output DrALU,
  output DrPC,
  output DrOFF,
  output LdPC,
  output LdIR,
  output LdMAR,
  output LdA,
  output LdB,
  output LdZ,
  output WrREG,
  output WrMEM,
  output [1:0] RegSel,
  output [1:0] func
);

  wire [1:0] bit_extender_1_out;
  wire [5:0] multiplexer_1_out, register_1_q, rom_1_data, rom_2_data;
  wire [24:0] rom_3_data;

  assign bit_extender_1_out = {{1{1'b0}}, Z};  // Bit_Extender bit_extender_1
  ROM #(.addrWidth(3), .dataWidth(6)) rom_1 (.addr(OPCODE), .data(rom_1_data));  // open: sel
  ROM #(.addrWidth(2), .dataWidth(6)) rom_2 (.addr(bit_extender_1_out), .data(rom_2_data));  // open: sel
  Multiplexer #(.select(2), .width(6), .enable("false")) multiplexer_1 (
    .in0(rom_3_data[5:0]), .in1(rom_1_data), .in2(rom_2_data), .out(multiplexer_1_out),
    .sel(rom_3_data[24:23]));  // open: in3
  Register #(.width(6)) register_1 (.D(multiplexer_1_out), .en(1'b1), .Q(register_1_q), .clk(CLK), .clr(CLR));
  ROM #(.addrWidth(6), .dataWidth(25)) rom_3 (
    .addr(register_1_q),
    .data({rom_3_data[24:23], func, RegSel, WrMEM, WrREG, LdZ, LdB, LdA, LdMAR, LdIR, LdPC, DrOFF, DrPC, DrALU, DrMEM, DrREG, rom_3_data[5:0]}));  // open: sel

  // Notes on the sheet:
  //   contents of rom_1 (hex, n*v repeats v):
  //   3 6 9 c 10 14 1b 1d
  //   contents of rom_2 (hex, n*v repeats v):
  //   0 18
  //   Jongyeon Kim
  //   903018469
  //   contents of rom_3 (hex, n*v repeats v):
  //   6201 1082 e00900 84044 108045 20100 84047 108048 220100 8404a 840b 20100 8404d 840e 210f 20080 84051
  //   8412 2113 40040 4055 88056 410117 1000000 4219 841a 900 a021c 840 1d
endmodule
